// Logisim project Domaci2.circ as structural Verilog: 4 circuits, main circuit Domaci2_mindnf
module Domaci2_mindnf (
  input  X1,
  input  X2,
  input  X3,
  input  X4,
  input  X5,
  output Y
);

  wire and_1_out, and_2_out, and_4_out, not_1_out, not_2_out, not_3_out, not_4_out;

  not not_1 (not_1_out, X1);
  and and_1 (and_1_out, not_1_out, X2);
  not not_2 (not_2_out, X3);
  not not_3 (not_3_out, X4);
  not not_4 (not_4_out, X5);
  and and_2 (and_2_out, and_1_out, not_2_out);
  and and_3 (Y, and_2_out, and_4_out);
  and and_4 (and_4_out, not_3_out, not_4_out);
endmodule

module Domaci2_minknf (
  input  X1,
  input  X2,
  input  X3,
  input  X4,
  input  X5,
  output Y
);

  wire and_1_out, and_2_out, and_4_out, not_1_out, not_2_out, not_3_out, not_4_out;

  not not_1 (not_1_out, X5);
  and and_1 (and_1_out, X2, not_1_out);
  not not_2 (not_2_out, X4);
  not not_3 (not_3_out, X3);
  not not_4 (not_4_out, X1);
  and and_2 (and_2_out, and_1_out, not_2_out);
  and and_3 (Y, and_2_out, and_4_out);
  and and_4 (and_4_out, not_3_out, not_4_out);
endmodule

module Domaci2_iskombinovano (
  input  in_1,
  input  in_2,
  input  in_3,
  input  in_4,
  input  in_5,
  output out_6
);

  Domaci2_redukovano_NOR domaci2_redukovano_nor_1 (.x1(in_1), .x2(in_2), .x3(in_3), .x4(in_4), .x5(in_5), .y(out_6));
endmodule

module Domaci2_redukovano_NOR (
  input  x1,
  input  x2,
  input  x3,
  input  x4,
  input  x5,
  output y
);

  wire nor_1_out, nor_2_out, nor_3_out, nor_4_out, nor_5_out, nor_6_out, nor_7_out;

  nor nor_1 (nor_1_out, x3, x1);
  nor nor_2 (nor_2_out, x2, x2);
  nor nor_3 (nor_3_out, nor_2_out, x5);
  nor nor_4 (nor_4_out, nor_3_out, nor_3_out);
  nor nor_5 (nor_5_out, nor_4_out, x4);
  nor nor_6 (nor_6_out, nor_5_out, nor_5_out);
  nor nor_7 (nor_7_out, nor_1_out, nor_1_out);
  nor nor_8 (y, nor_6_out, nor_7_out);

  // Notes on the sheet:
  //   Datum rodjenja  24.02. = 2+4+0+2 = 8
endmodule
