// Logisim project Ort_1_LogiSim_Vukasin_Paunovic_Domaci_1.circ as structural Verilog: 1 circuit, main circuit main
module main (
  input  in_1,
  input  in_2,
  input  in_3,
  input  in_4,
  input  in_5,
  input  in_6,
  input  in_7,
  input  in_8,
  input  in_9,
  input  in_10,
  input  in_11,
  input  in_12,
  input  in_13,
  input  in_14,
  input  in_15,
  input  in_16,
  input  in_17,
  input  in_18,
  output out_19
);

  wire not_1_out, not_2_out, not_3_out, not_4_out, not_5_out, not_6_out, not_7_out, not_8_out, not_9_out,
       xor_1_out, xor_2_out, xor_3_out, xor_4_out, xor_5_out, xor_6_out, xor_7_out, xor_8_out, xor_9_out;

  not not_1 (not_1_out, xor_1_out);
  xor xor_1 (xor_1_out, in_1, in_6);
  not not_2 (not_2_out, xor_2_out);
  xor xor_2 (xor_2_out, in_2, in_5);
  not not_3 (not_3_out, xor_3_out);
  xor xor_3 (xor_3_out, in_3, in_4);
  not not_4 (not_4_out, xor_4_out);
  xor xor_4 (xor_4_out, in_7, in_7);
  not not_5 (not_5_out, xor_5_out);
  xor xor_5 (xor_5_out, in_10, in_9);
  xor xor_6 (xor_6_out, in_11, in_11);
  not not_6 (not_6_out, xor_6_out);
  xor xor_7 (xor_7_out, in_16, in_15);
  not not_7 (not_7_out, xor_7_out);
  xor xor_8 (xor_8_out, in_17, in_14);
  not not_8 (not_8_out, xor_8_out);
  xor xor_9 (xor_9_out, in_18, in_13);
  not not_9 (not_9_out, xor_9_out);
  and and_1 (out_19, not_1_out, not_2_out, not_3_out, not_4_out, not_5_out, not_6_out, not_7_out, not_8_out, not_9_out);

  assign in_8 = in_7;
  assign in_12 = in_11;
endmodule
